# Fritzing sketch Untitled_Sketch (saved by Fritzing 0.9.2b)

parts:
  Composant1 = Arduino Uno (Rev3)  # not connected
  Composant2 = Base Shield V2
  Grove1 = Grove Buzz
  Grove_LED_Red1 = Grove LED Red
  Composant3 = Servo Improved
  Composant4 = Servo Improved
  Grove_Switch_(P)1 = Grove Switch (P)
  Grove_-_Bluetooth_/_BLE1 = Grove - Bluetooth / BLE

nets:
  N1: Composant2.pin_96, Grove_-_Bluetooth_/_BLE1.GND
  N2: Composant2.pin_97, Grove_-_Bluetooth_/_BLE1.VCC
  N3: Composant2.pin_98, Grove_-_Bluetooth_/_BLE1.Tx
  N4: Composant2.pin_99, Grove_-_Bluetooth_/_BLE1.Rx
  N5: Composant2.pin_104, Grove_Switch_(P)1.GND
  N6: Composant2.pin_105, Grove_Switch_(P)1.VCC
  N7: Composant2.pin_106, Grove_Switch_(P)1.NC
  N8: Composant2.pin_107, Grove_Switch_(P)1.SIG
  N9: Composant2.pin_108, Grove_LED_Red1.GND
  N10: Composant2.pin_109, Grove_LED_Red1.NC2
  N11: Composant2.pin_110, Grove_LED_Red1.NC1
  N12: Composant2.pin_111, Grove_LED_Red1.SIG
  N13: Composant2.pin_112, Grove1.GND
  N14: Composant2.pin_113, Grove1.VCC
  N15: Composant2.pin_115, Grove1.SIG
  N16: Composant2.pin_120, Composant3.ground, Composant4.ground
  VCC: Composant2.pin_121, Composant3.vcc, Composant4.vcc
  N17: Composant2.pin_122, Composant3.signal
  N18: Composant2.pin_123, Composant4.signal

custom parts:
  Grove LED Red: LED red, Grove connector.
  Grove Switch (P): Switch, Grove connector, panel mount.
